# Fritzing sketch Lab 2 (saved by Fritzing 0.9.3b)
breadboards: 2

parts:
  Part1 = Arduino Uno (Rev3) - ICSP
  U1 = 74HC595 SMD [package="SO16 [SMD]"]
  U2 = 74HC595 SMD [package="SO16 [SMD]"]
  Dot_Matrix1 = LED Dot Matrix 18mm (0.7 INCH)
  R1 = Resistor [tolerance=±5% resistance=220 package="2010 [SMD]"]
  R2 = Resistor [tolerance=±5% resistance=220 package="2010 [SMD]"]
  R3 = Resistor [tolerance=±5% resistance=220 package="2010 [SMD]"]
  R4 = Resistor [tolerance=±5% resistance=220 package="2010 [SMD]"]
  R5 = Resistor [tolerance=±5% resistance=220 package="2010 [SMD]"]
  R6 = Resistor [tolerance=±5% resistance=220 package="2010 [SMD]"]
  R8 = Resistor [tolerance=±5% resistance=220 package="2010 [SMD]"]
  R9 = Resistor [tolerance=±5% resistance=220 package="2010 [SMD]"]
  R10 = Resistor [tolerance=±5% resistance=220 package="2010 [SMD]"]
  R11 = Resistor [tolerance=±5% resistance=220 package="2010 [SMD]"]
  R12 = Resistor [tolerance=±5% resistance=220 package="2010 [SMD]"]
  R13 = Resistor [tolerance=±5% resistance=220 package="2010 [SMD]"]
  S1 = Momentary Switch [package=ksa_sealed_tac_switch]
  R14 = Resistor [tolerance=±5% resistance=220 package="2010 [SMD]"]

nets:
  VCC: Part1.5V, U1.MR, U1.VCC, U2.MR, U2.VCC, S1.3
  N1: Part1.D11_PWM/MOSI, U1.SH_CP, U2.SH_CP
  N2: Part1.D12/MISO, U1.ST_CP, U2.ST_CP
  N3: Part1.D13/SCK, U1.DS
  N4: Part1.D2, S1.2
  GND: Part1.GND, U1.GND, U1.OE, U2.GND, U2.OE, R14.Pin_1
  N5: U1.Q1, R2.Pin_1
  N6: U1.Q2, R3.Pin_1
  N7: U1.Q3, R6.Pin_0
  N8: U1.Q4, R5.Pin_0
  N9: U1.Q5, R4.Pin_0
  N10: U1.Q6, R8.Pin_0
  N11: U1.Q7, R9.Pin_0
  N12: U1.Q7', U2.DS
  N13: U1.Q0, R1.Pin_1
  N14: U2.Q1, R10.Pin_1
  N15: U2.Q2, R11.Pin_1
  N16: U2.Q3, R12.Pin_1
  N17: U2.Q0, R13.Pin_1
  N18: Dot_Matrix1.Column_1, R1.Pin_0
  N19: Dot_Matrix1.Row_3, R2.Pin_0
  N20: Dot_Matrix1.Column_2, R3.Pin_0
  N21: Dot_Matrix1.Row_5, R6.Pin_1
  N22: Dot_Matrix1.Row_6, R5.Pin_1
  N23: Dot_Matrix1.Row_7, R4.Pin_1
  N24: Dot_Matrix1.Column_4, R8.Pin_1
  N25: Dot_Matrix1.Column_5, R9.Pin_1
  N26: Dot_Matrix1.Row_4, R13.Pin_0
  N27: Dot_Matrix1.Column_3, R10.Pin_0
  N28: Dot_Matrix1.Row_2, R11.Pin_0
  N29: Dot_Matrix1.Row_1, R12.Pin_0
  N30: S1.1, R14.Pin_0
