# Fritzing sketch Lab_3_A (saved by Fritzing 0.9.3b)
breadboards: 1

parts:
  Part1 = Arduino Uno (Rev3) - ICSP
  hc-sr1 = hc-sr04  # not connected
  LED2 = smd LED [color="Green (555nm)" package="0603 [SMD]"]  # not connected
  R1 = Photocell (LDR) [package=THT]
  R2 = Resistor [tolerance=±5% resistance=330 package=THT]  # not connected
  R3 = Resistor [tolerance=±5% resistance=330 package=THT]
  R4 = Resistor [tolerance=±5% resistance=330 package=THT]
  LED3 = LED - 5mm [color="Red (633nm)" package="5 mm [THT]"]

nets:
  N1: Part1.A0, R1.pin_0, R3.Pin_1
  N2: Part1.D11_PWM/MOSI, R4.Pin_0
  N3: Part1.5V, R1.pin_1
  N4: Part1.GND, R3.Pin_0, LED3.cathode
  N5: R4.Pin_1, LED3.anode
