# Fritzing sketch Lab_3_B (saved by Fritzing 0.9.3b)
breadboards: 1

parts:
  Part2 = Arduino Uno (Rev3) - ICSP
  hc-sr2 = hc-sr04  # not connected
  LED4 = smd LED [color="Green (555nm)" package="0603 [SMD]"]
  R5 = Photocell (LDR) [package=THT]
  R6 = Resistor [tolerance=±5% resistance=330 package=THT]
  R7 = Resistor [tolerance=±5% resistance=330 package=THT]
  R8 = Resistor [tolerance=±5% resistance=330 package=THT]
  LED5 = LED - 5mm [color="Red (633nm)" package="5 mm [THT]"]

nets:
  N1: Part2.A0, R5.pin_0, R7.Pin_1
  N2: Part2.D10_PWM/SS, R8.Pin_1
  N3: Part2.D11_PWM/MOSI, R6.Pin_0
  N4: Part2.5V, R5.pin_1
  N5: Part2.GND, LED4.cathode, R7.Pin_0, LED5.cathode
  N6: LED4.anode, R8.Pin_0
  N7: R6.Pin_1, LED5.anode
