# Fritzing sketch Lab_3_C (saved by Fritzing 0.9.3b)
breadboards: 1

parts:
  Part1 = Arduino Uno (Rev3) - ICSP
  RE1 = Rotary Encoder [package=THT]  # not connected
  Part2 = SPI OLED Monochrome 128x64 0.96 inch

nets:
  N1: Part1.ICSP_MISO, Part1.D12/MISO, Part2.DC
  N2: Part1.D9_PWM, Part2.SCK
  N3: Part1.D10_PWM/SS, Part2.SDA
  N4: Part1.D11_PWM/MOSI, Part2.RES
  N5: Part1.D13/SCK, Part2.CS
  5V: Part1.5V, Part2.VDD
  GND: Part1.GND, Part2.GND

custom parts:
  SPI OLED Monochrome 128x64 0.96 inch: Unknown 128x64 0.96 inch 128x64 SPI Monochrome OLED display
